# Fritzing sketch Overview (saved by Fritzing 0.9.3b)

parts:
  Part1 = Arduino Uno (Rev3) - ICSP
  S1 = H-Bridge with L298N
  S2 = H-Bridge with L298N
  S3 = H-Bridge with L298N
  S4 = H-Bridge with L298N
  J1 = Basic Servo
  J2 = Basic Servo
  M1 = DC Motor
  M2 = DC Motor
  M3 = DC Motor
  M4 = DC Motor
  M5 = Stepper Motor - Bipolar
  M6 = Stepper Motor - Bipolar
  Power_plug1 = Power plug
  ENCODER = female pin header, 4 pins [form="♀ (female)"]

nets:
  N1: Part1.A0, S2.IN1, S4.IN1
  N2: Part1.A1, S2.ENA, S2.ENB, S4.ENA, S4.ENB
  N3: Part1.A3, ENCODER.pin3
  N4: Part1.A4/SDA, ENCODER.pin4
  N5: Part1.ICSP_MOSI, Part1.D11_PWM/MOSI, S2.IN4, S4.IN4
  N6: Part1.D8, S1.IN2, S1.IN4, S3.IN2, S3.IN4
  N7: Part1.D9_PWM, J1.pulse
  N8: Part1.D10_PWM/SS, J2.pulse
  N9: Part1.D12/MISO, S2.IN3, S4.IN3
  N10: Part1.D13/SCK, S2.IN2, S4.IN2
  N11: Part1.D6_PWM, S1.ENA, S1.ENB, S3.ENA, S3.ENB
  N12: Part1.D7, S1.IN1, S1.IN3, S3.IN1, S3.IN3
  N13: Part1.5V, ENCODER.pin1
  GND: Part1.GND, S2.GND, S4.GND, J1.gnd, J2.gnd, Power_plug1.GND, ENCODER.pin2
  12V: Part1.VIN, S2.12V, S4.12V, Power_plug1.VCC
  N14: S1.M1-01, M2.pin_2
  N15: S1.M1-02, M2.pin_1
  N16: S1.M2-01, M1.pin_2
  N17: S1.M2-02, M1.pin_1
  N18: S2.M1-01, M6.C
  N19: S2.M1-02, M6.A
  N20: S2.M2-01, M6.D
  N21: S2.M2-02, M6.B
  N22: S3.M1-01, M4.pin_2
  N23: S3.M1-02, M4.pin_1
  N24: S3.M2-01, M3.pin_2
  N25: S3.M2-02, M3.pin_1
  N26: S4.M1-01, M5.C
  N27: S4.M1-02, M5.A
  N28: S4.M2-01, M5.D
  N29: S4.M2-02, M5.B

custom parts:
  H-Bridge with L298N: h-bridge
